// Logisim project drisc.circ as structural Verilog: 15 circuits, main circuit main
module main (
);

  wire address_selector_1_read_out, address_selector_1_write_out, address_selector_2_read_out,
       address_selector_3_write_out, address_selector_4_write_out, address_selector_5_read_out,
       address_selector_5_write_out, ALU_Use_PC, and_1_out, and_2_out, button_1_out, button_2_out,
       button_3_out, button_4_out, button_5_out, button_6_out, button_7_out, button_8_out, Cl0ck,
       comparator_1_eq, csr_controller_1_system_jump, Forward_Address, IO_Read, IO_Write, keyboard_1_avail,
       Load_Upper_Immediate, or_1_out, Pad_Read, Pad_Write, PC_Jump, PC_Read_Next, PC_Relative,
       PC_Use_Offset, Phase1, Phase2, Read_CSR, real_time_device_1_timer_interrupt, Register_File_Write,
       Reset, Software_Interrupt_Reg_q, System_Load, undriven_3, Use_Immediate;
  wire [1:0] Data_Offset, Pad_Data_Size;
  wire [2:0] Data_Type;
  wire [3:0] ALUComponent_cnzv, undriven, undriven_2;
  wire [4:0] OP_Function;
  wire [6:0] keyboard_1_data, OperationController_opcode;
  wire [7:0] s_r_ff_8_q;
  wire [7:7] not_1_out;
  wire [9:0] OperationController_current_decoded_instruction;
  wire [14:0] Register_Addresses;
  wire [15:0] random_1_out;
  wire [31:0] address_selector_1_address_out, address_selector_3_address_out, address_selector_5_address_out,
       ALUComponent_result, controlled_buffer_1_out, csr_controller_1_c_bus,
       csr_controller_1_system_target_address, DataIO_cpu_out, multiplexer_1_out, multiplexer_2_out,
       multiplexer_3_out, multiplexer_4_out, OperationController_current_instruction_out,
       OperationController_immediate, ProgramCounter_address_bus_out, ProgramCounter_calculated_address,
       ProgramCounter_current_out, ProgramCounter_next_out, real_time_device_1_data_out,
       RegisterFile_a_bus_out, RegisterFile_b_bus_out;

  // Probe on Register_Addresses[4:0]
  // Probe on Register_Addresses[9:5]
  // Probe on Register_Addresses[14:10]
  Register_File RegisterFile (
    .C_Bus_In(multiplexer_1_out), .Addresses_In(Register_Addresses), .Write(Register_File_Write),
    .Clock(Cl0ck), .Reset(Reset), .A_Bus_Out(RegisterFile_a_bus_out), .B_Bus_Out(RegisterFile_b_bus_out));
  // Probe on RegisterFile_a_bus_out
  // Probe on RegisterFile_b_bus_out
  // Probe on multiplexer_1_out
  Multiplexer #(.width(32)) multiplexer_1 (
    .in0(multiplexer_2_out), .in1(DataIO_cpu_out), .out(multiplexer_1_out), .sel(IO_Read));
  Input_Buffer DataIO (
    .IO_In(controlled_buffer_1_out), .Write(IO_Write), .Clock(Cl0ck), .Data_Offset(Data_Offset),
    .Data_Type(Data_Type), .CPU_Out(DataIO_cpu_out));
  Multiplexer #(.width(32)) multiplexer_2 (
    .in0(multiplexer_3_out), .in1(OperationController_immediate), .out(multiplexer_2_out),
    .sel(Load_Upper_Immediate));
  Multiplexer #(.width(32)) multiplexer_3 (
    .in0(multiplexer_4_out), .in1(ProgramCounter_next_out), .out(multiplexer_3_out), .sel(PC_Read_Next));
  T_Flip_Flop t_ff_1 (.clk(Cl0ck), .T(1'b1), .Q(Phase1), .Qn(Phase2), .reset(Reset));  // open: preset
  ALU ALUComponent (
    .Operation(OP_Function), .Use_PC(ALU_Use_PC), .Use_Immediate(Use_Immediate), .a(RegisterFile_a_bus_out),
    .Program_Counter_In(ProgramCounter_current_out), .b(RegisterFile_b_bus_out),
    .Immediate(OperationController_immediate), .Result(ALUComponent_result), .CNZV(ALUComponent_cnzv));  // open: Source1, Source2
  // Probe on nothing
  // Probe on nothing
  Multiplexer #(.width(32)) multiplexer_4 (
    .in0(ALUComponent_result), .in1(csr_controller_1_c_bus), .out(multiplexer_4_out), .sel(Read_CSR));
  Operation_Controller OperationController (
    .Data_In(controlled_buffer_1_out), .System_Load(System_Load), .Phase1(Phase1), .Phase2(Phase2),
    .CNZV(ALUComponent_cnzv), .Clock(Cl0ck), .Reset(Reset), .OPCode(OperationController_opcode),
    .Current_Instruction_Out(OperationController_current_instruction_out), .Data_Type(Data_Type),
    .Register_Adresses(Register_Addresses), .Immediate(OperationController_immediate),
    .Current_Decoded_Instruction(OperationController_current_decoded_instruction),
    .PC_Use_Offset(PC_Use_Offset), .PC_Forward_Address(Forward_Address),
    .Register_File_Write(Register_File_Write), .PC_Read_Next(PC_Read_Next), .PC_Relative(PC_Relative),
    .Load_Upper_Immediate(Load_Upper_Immediate), .PC_Jump(PC_Jump), .Use_Immediate(Use_Immediate),
    .ALU_Use_PC(ALU_Use_PC), .Data_IO_Write(IO_Write), .PAD_Read(Pad_Read), .OP_Function(OP_Function),
    .Data_IO_Read(IO_Read), .PAD_Data_Size(Pad_Data_Size), .PAD_Write(Pad_Write));
  // Probe on OperationController_opcode
  // Probe on ProgramCounter_current_out
  // Probe on OperationController_immediate
  CSR_Controller csr_controller_1 (
    .Reset(Reset), .Clock(Cl0ck), .A_Bus(RegisterFile_a_bus_out), .Current_PC(ProgramCounter_current_out),
    .Pad_Software_Interrupt(Software_Interrupt_Reg_q),
    .Pad_Timer_Interrupt(real_time_device_1_timer_interrupt), .Pad_External_Interrupt(keyboard_1_avail),
    .PC_Jump(PC_Jump), .Current_Decoded_Instruction(OperationController_current_decoded_instruction),
    .Current_Instruction(OperationController_current_instruction_out),
    .Calculated_Address(ProgramCounter_calculated_address), .Phase1(Phase1), .Phase2(Phase2),
    .Read_CSR(Read_CSR), .System_Load(System_Load), .System_Jump(csr_controller_1_system_jump),
    .System_Target_Address(csr_controller_1_system_target_address), .C_Bus(csr_controller_1_c_bus));
  Program_Counter ProgramCounter (
    .Forward_Address(Forward_Address), .PC_Relative(PC_Relative), .Address_In(RegisterFile_a_bus_out),
    .Immediate(OperationController_immediate),
    .System_Target_Address(csr_controller_1_system_target_address), .Jump(PC_Jump),
    .System_Jump(csr_controller_1_system_jump), .Reset(Reset), .Clock(Cl0ck), .Write(Phase2),
    .Use_Offset(PC_Use_Offset), .System_Load(System_Load), .Address_Bus_Out(ProgramCounter_address_bus_out),
    .Byte_Offset(Data_Offset), .Next_Out(ProgramCounter_next_out), .Current_Out(ProgramCounter_current_out),
    .Calculated_Address(ProgramCounter_calculated_address));  // open: Last_Out
  assign controlled_buffer_1_out = Pad_Write ? RegisterFile_b_bus_out : 32'bz;  // Controlled_Buffer controlled_buffer_1
  // Probe on controlled_buffer_1_out
  // Probe on ProgramCounter_address_bus_out
  Clock MainClock (.out(Cl0ck));
  POR #(.PorHighDuration(1), .porsize(2)) por_1 (.out(Reset));
  Comparator #(.width(32)) comparator_1 (
    .a(ProgramCounter_address_bus_out), .b(32'h81000010), .eq(comparator_1_eq));  // open: gt, lt
  Address_Selector address_selector_1 (
    .Read_In(Pad_Read), .Write_In(Pad_Write), .Address_In(ProgramCounter_address_bus_out),
    .Min_Address({32{1'b0}}), .Max_Address(32'hfffffc), .Read_Out(address_selector_1_read_out),
    .Write_Out(address_selector_1_write_out), .Address_Out(address_selector_1_address_out));
  // RAM #(.addrWidth(24), .databus("bidir"), .enables("line"), .line("quad"), .misaligned("true"), .\type ("nonvolatile")) ram_1: pin names not known; wires that end beside it: address_selector_1_address_out[23:0], address_selector_1_write_out, address_selector_1_read_out, 1'b1, Pad_Data_Size[1], Cl0ck
  Keyboard keyboard_1 (
    .clk(Cl0ck), .re(address_selector_2_read_out), .avail(keyboard_1_avail), .data(keyboard_1_data));  // open: clr
  Address_Selector address_selector_2 (
    .Read_In(Pad_Read), .Write_In(Pad_Write), .Address_In(ProgramCounter_address_bus_out),
    .Min_Address(32'hfffffc), .Max_Address(32'h1000000), .Read_Out(address_selector_2_read_out));  // open: Write_Out, Address_Out
  Address_Selector address_selector_3 (
    .Write_In(Pad_Write), .Address_In(ProgramCounter_address_bus_out), .Min_Address(32'h1000000),
    .Max_Address(32'h1100000), .Write_Out(address_selector_3_write_out),
    .Address_Out(address_selector_3_address_out));  // open: Read_In, Read_Out
  Address_Selector address_selector_4 (
    .Write_In(Pad_Write), .Address_In(ProgramCounter_address_bus_out), .Min_Address(32'h1100000),
    .Max_Address(32'h1100001), .Write_Out(address_selector_4_write_out));  // open: Read_In, Read_Out, Address_Out
  assign controlled_buffer_1_out = address_selector_5_read_out ? real_time_device_1_data_out : 32'bz;  // Controlled_Buffer controlled_buffer_2
  Address_Selector address_selector_5 (
    .Read_In(Pad_Read), .Write_In(Pad_Write), .Address_In(ProgramCounter_address_bus_out),
    .Min_Address(32'h81000000), .Max_Address(32'h81000010), .Read_Out(address_selector_5_read_out),
    .Write_Out(address_selector_5_write_out), .Address_Out(address_selector_5_address_out));
  and and_1 (and_1_out, comparator_1_eq, Pad_Write);
  Register #(.width(1)) Software_Interrupt_Reg (
    .D(controlled_buffer_1_out[0]), .en(and_1_out), .clk(Cl0ck), .Q(Software_Interrupt_Reg_q), .clr(Reset));
  not not_1 (not_1_out[7], keyboard_1_avail);
  Joystick joystick_1 ();  // open: x, y
  assign controlled_buffer_1_out = address_selector_2_read_out ? {not_1_out[7], keyboard_1_data, undriven_2, undriven, random_1_out} : 32'bz;  // Controlled_Buffer controlled_buffer_3
  Real_Time_Device real_time_device_1 (
    .Clock(Cl0ck), .Reset(Reset), .Address(address_selector_5_address_out[3:2]),
    .Write(address_selector_5_write_out), .Data_In(controlled_buffer_1_out),
    .Timer_Interrupt(real_time_device_1_timer_interrupt), .Data_Out(real_time_device_1_data_out));
  Random random_1 (.next(address_selector_2_read_out), .clk(Cl0ck), .out(random_1_out[7:0]));  // open: clr
  // DipSwitch dipswitch_1: pin names not known
  // RGB_Video #(.cursor("No Cursor"), .height(64), .scale(6), .width(64)) rgb_video_1: pin names not known; wires that end beside it: Reset, Cl0ck, address_selector_3_write_out, address_selector_3_address_out[5:0], address_selector_3_address_out[11:6], controlled_buffer_1_out[23:0]
  Button button_1 (.out(button_1_out));
  TTY #(.rows(12)) tty_1 (
    .data(controlled_buffer_1_out[6:0]), .clk(Cl0ck), .we(address_selector_4_write_out), .clr(or_1_out));
  and and_2 (and_2_out, controlled_buffer_1_out[7], address_selector_4_write_out);
  Button button_2 (.out(button_2_out));
  S_R_Flip_Flop #(.trigger("high")) s_r_ff_1 (
    .S(button_1_out), .clk(Cl0ck), .R(undriven_3), .Q(s_r_ff_8_q[7]), .reset(Reset));  // open: Qn, preset
  S_R_Flip_Flop #(.trigger("high")) s_r_ff_2 (
    .S(button_2_out), .clk(Cl0ck), .R(undriven_3), .Q(s_r_ff_8_q[6]), .reset(Reset));  // open: Qn, preset
  or or_1 (or_1_out, and_2_out, Reset);
  Button button_3 (.out(button_3_out));
  Button button_4 (.out(button_4_out));
  S_R_Flip_Flop #(.trigger("high")) s_r_ff_3 (
    .S(button_3_out), .clk(Cl0ck), .R(undriven_3), .Q(s_r_ff_8_q[5]), .reset(Reset));  // open: Qn, preset
  Button button_5 (.out(button_5_out));
  S_R_Flip_Flop #(.trigger("high")) s_r_ff_4 (
    .S(button_4_out), .clk(Cl0ck), .R(undriven_3), .Q(s_r_ff_8_q[4]), .reset(Reset));  // open: Qn, preset
  Button button_6 (.out(button_6_out));
  S_R_Flip_Flop #(.trigger("high")) s_r_ff_5 (
    .S(button_5_out), .clk(Cl0ck), .R(undriven_3), .Q(s_r_ff_8_q[3]), .reset(Reset));  // open: Qn, preset
  S_R_Flip_Flop #(.trigger("high")) s_r_ff_6 (
    .S(button_6_out), .clk(Cl0ck), .R(undriven_3), .Q(s_r_ff_8_q[2]), .reset(Reset));  // open: Qn, preset
  Button button_7 (.out(button_7_out));
  Button button_8 (.out(button_8_out));
  S_R_Flip_Flop #(.trigger("high")) s_r_ff_7 (
    .S(button_7_out), .clk(Cl0ck), .R(undriven_3), .Q(s_r_ff_8_q[1]), .reset(Reset));  // open: Qn, preset
  S_R_Flip_Flop #(.trigger("high")) s_r_ff_8 (
    .S(button_8_out), .clk(Cl0ck), .R(undriven_3), .Q(s_r_ff_8_q[0]), .reset(Reset));  // open: Qn, preset

  // Notes on the sheet:
  //   <Processor     Input Output Devices>
  //   Data Bus
  //   (IO Bus)
  //   Address Bus
  //   Keyboard
  //   Joystick
  //   Switches
  //   Buttons
endmodule

module ALU (
  input  [4:0] Operation,
  input  Use_PC,
  input  [31:0] a,
  input  [31:0] Program_Counter_In,
  input  Use_Immediate,
  input  [31:0] b,
  input  [31:0] Immediate,
  output [3:0] CNZV,
  output [31:0] Result,
  output [31:0] Source1,
  output [31:0] Source2
);

  wire and_1_out, comparator_1_lt, comparator_2_lt, or_1_out, xnor_1_out, xor_3_out, xor_4_out;
  wire [1:0] and_3_out;
  wire [1:1] and_2_out;
  wire [31:0] adder_1_out, and_4_out, bit_extender_1_out, bit_extender_2_out, bit_extender_3_out,
       multiplexer_3_out, multiplication_1_r_high, multiplication_1_r_low, or_2_out, shifter_1_out,
       shifter_2_out, shifter_3_out, xor_1_out, xor_2_out;

  or or_1 (or_1_out, Operation[2], ~Operation[4]);  // OR_Gate
  Multiplexer #(.width(32)) multiplexer_1 (.in0(a), .in1(Program_Counter_In), .out(Source1), .sel(Use_PC));
  Multiplexer #(.width(32)) multiplexer_2 (.in0(b), .in1(Immediate), .out(Source2), .sel(Use_Immediate));
  and and_1 (and_1_out, Operation[0], ~Operation[1], ~Operation[3], or_1_out);  // AND_Gate
  and and_2 (and_2_out[1], ~and_1_out, Use_Immediate);  // AND_Gate
  assign and_3_out = Operation[4:3] & ~{2{and_2_out[1]}};  // AND_Gate and_3, 2 bits wide
  assign or_2_out = Source1 | Source2;  // OR_Gate or_2, 32 bits wide
  assign and_4_out = Source1 & Source2;  // AND_Gate and_4, 32 bits wide
  assign bit_extender_1_out = {{31{and_3_out[1]}}, and_3_out[1]};  // Bit_Extender bit_extender_1
  Shifter #(.width(32)) shifter_1 (.in(Source1), .\dist (Source2[4:0]), .out(shifter_1_out));
  assign bit_extender_2_out = {{31{1'b0}}, comparator_1_lt};  // Bit_Extender bit_extender_2
  Comparator #(.width(32)) comparator_1 (.a(Source1), .b(Source2), .lt(comparator_1_lt));  // open: gt, eq
  assign bit_extender_3_out = {{31{1'b0}}, comparator_2_lt};  // Bit_Extender bit_extender_3
  Comparator #(.mode("unsigned"), .width(32)) comparator_2 (
    .a(Source1), .b(Source2), .lt(comparator_2_lt));  // open: gt, eq
  assign xor_1_out = Source1 ^ Source2;  // XOR_Gate xor_1, 32 bits wide
  Shifter #(.shift("lr"), .width(32)) shifter_2 (.in(Source1), .\dist (Source2[4:0]), .out(shifter_2_out));
  Shifter #(.shift("ar"), .width(32)) shifter_3 (.in(Source1), .\dist (Source2[4:0]), .out(shifter_3_out));
  Multiplication multiplication_1 (
    .Sign(Operation[1:0]), .A(Source1), .B(Source2), .R_Low(multiplication_1_r_low),
    .R_High(multiplication_1_r_high));
  Adder #(.width(32)) adder_1 (.a(Source1), .b(xor_2_out), .out(adder_1_out), .cin(and_3_out[1]), .cout(CNZV[0]));
  assign xor_2_out = bit_extender_1_out ^ Source2;  // XOR_Gate xor_2, 32 bits wide
  Multiplexer #(.width(32)) multiplexer_3 (
    .in0(shifter_2_out), .in1(shifter_3_out), .out(multiplexer_3_out), .sel(and_3_out[1]));
  Multiplexer #(.select(4), .width(32)) multiplexer_4 (
    .in0(adder_1_out), .in1(shifter_1_out), .in2(bit_extender_2_out), .in3(bit_extender_3_out),
    .in4(xor_1_out), .in5(multiplexer_3_out), .in6(or_2_out), .in7(and_4_out), .in8(multiplication_1_r_low),
    .in9(multiplication_1_r_high), .in10(multiplication_1_r_high), .in11(multiplication_1_r_high),
    .in12({32{1'b0}}), .in13({32{1'b0}}), .in14({32{1'b0}}), .in15({32{1'b0}}),
    .out({CNZV[1], Result[30:0]}), .sel({and_3_out[0], Operation[2:0]}));
  xor xor_3 (xor_3_out, CNZV[1], Source1[31]);
  xnor xnor_1 (xnor_1_out, Source1[31], Source2[31]);
  nor nor_1 (CNZV[2], Result[0], Result[1], Result[2], Result[3], Result[4], Result[5], Result[6], Result[7], Result[8], Result[9], Result[10], Result[11], Result[12], Result[13], Result[14], Result[15], Result[16], Result[17], Result[18], Result[19], Result[20], Result[21], Result[22], Result[23], Result[24], Result[25], Result[26], Result[27], Result[28], Result[29], Result[30], CNZV[1]);
  xor xor_4 (xor_4_out, xnor_1_out, and_3_out[1]);
  and and_5 (CNZV[3], xor_3_out, xor_4_out);

  assign Result[31] = CNZV[1];

  // Notes on the sheet:
  //   a: initial=0xffffffff
  //   if(~(operation == 1 | operation == 5 | operation = 21) & use_immediate) operation[4:3] = 2'b0
  //   \/
endmodule

module Program_Counter (
  input  Write,
  input  Jump,
  input  System_Jump,
  input  Reset,
  input  Clock,
  input  PC_Relative,
  input  [31:0] Address_In,
  input  [31:0] Immediate,
  input  Use_Offset,
  input  [31:0] System_Target_Address,
  input  System_Load,
  input  Forward_Address,
  output [31:0] Last_Out,
  output [31:0] Current_Out,
  output [31:0] Next_Out,
  output [31:0] Calculated_Address,
  output [31:0] Address_Bus_Out,
  output [1:0] Byte_Offset
);

  wire and_1_out, or_1_out;
  wire [1:0] and_2_out;
  wire [31:0] multiplexer_1_out, multiplexer_2_out, multiplexer_3_out;

  Multiplexer #(.width(32)) multiplexer_1 (
    .in0(Address_In), .in1({Current_Out[31:2], 2'b00}), .out(multiplexer_1_out), .sel(PC_Relative));
  Adder #(.width(32)) adder_1 (.a(multiplexer_1_out), .b(Immediate), .out(Calculated_Address));  // open: cin, cout
  or or_1 (or_1_out, Jump, System_Jump);
  Multiplexer #(.width(32)) multiplexer_2 (
    .in0(Calculated_Address), .in1(System_Target_Address), .out(multiplexer_2_out), .sel(System_Jump));
  and and_1 (and_1_out, Write, ~or_1_out);  // AND_Gate
  Counter #(.max('h3fffffff), .width(30)) Next_Counter (
    .load(or_1_out), .D(multiplexer_2_out[31:2]), .count(and_1_out), .Q(Next_Out[31:2]), .clk(Clock),
    .clr(Reset));  // open: carry, up
  assign and_2_out = multiplexer_2_out[1:0] & {2{Use_Offset}};  // AND_Gate and_2, 2 bits wide
  Register #(.width(30)) Current (.D(Next_Out[31:2]), .en(Write), .clk(Clock), .Q(Current_Out[31:2]), .clr(Reset));
  Multiplexer #(.width(32)) multiplexer_3 (
    .in0({multiplexer_2_out[31:2], and_2_out}), .in1(System_Target_Address), .out(multiplexer_3_out),
    .sel(System_Load));
  Multiplexer #(.width(32)) multiplexer_4 (
    .in0({Next_Out[31:2], 2'b00}), .in1(multiplexer_3_out), .out(Address_Bus_Out), .sel(Forward_Address));
  Register #(.width(2)) Byte_Offset_Reg (
    .D(multiplexer_2_out[1:0]), .en(Forward_Address), .clk(Clock), .Q(Byte_Offset), .clr(Reset));
  Register #(.width(30)) Last (.D(Current_Out[31:2]), .en(Write), .clk(Clock), .Q(Last_Out[31:2]), .clr(Reset));

  assign Current_Out[1:0] = 2'b00;
  assign Last_Out[1:0] = 2'b00;
  assign Next_Out[1:0] = 2'b00;

  // Other names for the same wires on the sheet: Current_PC[31:2] = Current_Out[31:2]
endmodule

module Input_Buffer (
  input  [2:0] Data_Type,
  input  [1:0] Data_Offset,
  input  [31:0] IO_In,
  input  Write,
  input  Clock,
  output [31:0] CPU_Out
);

  wire and_1_out, and_2_out, not_1_out;
  wire [7:0] Input_Register_q, Input_Register_q_2, Input_Register_q_3, Input_Register_q_4, multiplexer_1_out;
  wire [15:0] multiplexer_2_out, multiplexer_3_out;
  wire [31:0] bit_extender_1_out, bit_extender_2_out, multiplexer_4_out;

  Register #(.width(32)) Input_Register (
    .D(IO_In), .en(Write), .clk(Clock),
    .Q({Input_Register_q_4, Input_Register_q_3, Input_Register_q_2, Input_Register_q}));  // open: clr
  Multiplexer #(.select(2), .width(8)) multiplexer_1 (
    .in0(Input_Register_q), .in1(Input_Register_q_2), .in2(Input_Register_q_3), .in3(Input_Register_q_4),
    .out(multiplexer_1_out), .sel(Data_Offset));
  Multiplexer #(.width(16)) multiplexer_2 (
    .in0({Input_Register_q_2, Input_Register_q}), .in1({Input_Register_q_3, Input_Register_q_2}),
    .out(multiplexer_2_out), .sel(Data_Offset[0]));
  Multiplexer #(.width(16)) multiplexer_3 (
    .in0(multiplexer_2_out), .in1({Input_Register_q_4, Input_Register_q_3}), .out(multiplexer_3_out),
    .sel(Data_Offset[1]));
  not not_1 (not_1_out, Data_Type[2]);
  and and_1 (and_1_out, multiplexer_1_out[7], not_1_out);
  assign bit_extender_1_out = {{24{and_1_out}}, multiplexer_1_out};  // Bit_Extender bit_extender_1
  and and_2 (and_2_out, multiplexer_3_out[15], not_1_out);
  assign bit_extender_2_out = {{16{and_2_out}}, multiplexer_3_out};  // Bit_Extender bit_extender_2
  Multiplexer #(.width(32)) multiplexer_4 (
    .in0(bit_extender_1_out), .in1(bit_extender_2_out), .out(multiplexer_4_out), .sel(Data_Type[0]));
  Multiplexer #(.width(32)) multiplexer_5 (
    .in0(multiplexer_4_out),
    .in1({Input_Register_q_4, Input_Register_q_3, Input_Register_q_2, Input_Register_q}), .out(CPU_Out),
    .sel(Data_Type[1]));

  // Notes on the sheet:
  //   IO_In: initial=0xf2f2f2f2
endmodule

module Register_File (
  input  [14:0] Addresses_In,
  input  [31:0] C_Bus_In,
  input  Write,
  input  Clock,
  input  Reset,
  output [31:0] A_Bus_Out,
  output [31:0] B_Bus_Out
);

  Register_Bank IntRegisterBank (
    .Address_A(Addresses_In[9:5]), .Address_B(Addresses_In[14:10]), .Data_In(C_Bus_In), .Clock(Clock),
    .Address_C(Addresses_In[4:0]), .Write_Enable(Write), .Reset(Reset), .A_Data_Out(A_Bus_Out),
    .B_Data_Out(B_Bus_Out));
endmodule

module Register_Bank (
  input  [4:0] Address_A,
  input  Reset,
  input  [31:0] Data_In,
  input  Clock,
  input  [4:0] Address_C,
  input  [4:0] Address_B,
  input  Write_Enable,
  output [31:0] A_Data_Out,
  output [31:0] B_Data_Out
);

  wire [31:0] decoder_1_out0, x1_q, x2_q, x3_q, x4_q, x5_q, x6_q, x7_q, x8_q, x9_q, x10_q, x11_q, x12_q,
       x13_q, x14_q, x15_q, x16_q, x17_q, x18_q, x19_q, x20_q, x21_q, x22_q, x23_q, x24_q, x25_q, x26_q,
       x27_q, x28_q, x29_q, x30_q, x31_q;

  Decoder #(.select(5)) decoder_1 (
    .out0(decoder_1_out0[0]), .out1(decoder_1_out0[1]), .out2(decoder_1_out0[2]), .out3(decoder_1_out0[3]),
    .out4(decoder_1_out0[4]), .out5(decoder_1_out0[5]), .out6(decoder_1_out0[6]), .out7(decoder_1_out0[7]),
    .out8(decoder_1_out0[8]), .out9(decoder_1_out0[9]), .out10(decoder_1_out0[10]),
    .out11(decoder_1_out0[11]), .out12(decoder_1_out0[12]), .out13(decoder_1_out0[13]),
    .out14(decoder_1_out0[14]), .out15(decoder_1_out0[15]), .out16(decoder_1_out0[16]),
    .out17(decoder_1_out0[17]), .out18(decoder_1_out0[18]), .out19(decoder_1_out0[19]),
    .out20(decoder_1_out0[20]), .out21(decoder_1_out0[21]), .out22(decoder_1_out0[22]),
    .out23(decoder_1_out0[23]), .out24(decoder_1_out0[24]), .out25(decoder_1_out0[25]),
    .out26(decoder_1_out0[26]), .out27(decoder_1_out0[27]), .out28(decoder_1_out0[28]),
    .out29(decoder_1_out0[29]), .out30(decoder_1_out0[30]), .out31(decoder_1_out0[31]), .sel(Address_C),
    .en(Write_Enable));
  // NoConnect on Data_In
  // NoConnect on decoder_1_out0[0]
  // NoConnect on Clock
  Register #(.width(32)) x2 (.D(Data_In), .en(decoder_1_out0[2]), .clk(Clock), .Q(x2_q), .clr(Reset));
  Register #(.width(32)) x4 (.D(Data_In), .en(decoder_1_out0[4]), .clk(Clock), .Q(x4_q), .clr(Reset));
  Register #(.width(32)) x6 (.D(Data_In), .en(decoder_1_out0[6]), .clk(Clock), .Q(x6_q), .clr(Reset));
  Register #(.width(32)) x8 (.D(Data_In), .en(decoder_1_out0[8]), .clk(Clock), .Q(x8_q), .clr(Reset));
  Register #(.width(32)) x10 (.D(Data_In), .en(decoder_1_out0[10]), .clk(Clock), .Q(x10_q), .clr(Reset));
  Register #(.width(32)) x12 (.D(Data_In), .en(decoder_1_out0[12]), .clk(Clock), .Q(x12_q), .clr(Reset));
  Register #(.width(32)) x14 (.D(Data_In), .en(decoder_1_out0[14]), .clk(Clock), .Q(x14_q), .clr(Reset));
  Register #(.width(32)) x16 (.D(Data_In), .en(decoder_1_out0[16]), .clk(Clock), .Q(x16_q), .clr(Reset));
  Register #(.width(32)) x18 (.D(Data_In), .en(decoder_1_out0[18]), .clk(Clock), .Q(x18_q), .clr(Reset));
  Register #(.width(32)) x20 (.D(Data_In), .en(decoder_1_out0[20]), .clk(Clock), .Q(x20_q), .clr(Reset));
  Register #(.width(32)) x22 (.D(Data_In), .en(decoder_1_out0[22]), .clk(Clock), .Q(x22_q), .clr(Reset));
  Register #(.width(32)) x24 (.D(Data_In), .en(decoder_1_out0[24]), .clk(Clock), .Q(x24_q), .clr(Reset));
  Register #(.width(32)) x26 (.D(Data_In), .en(decoder_1_out0[26]), .clk(Clock), .Q(x26_q), .clr(Reset));
  Register #(.width(32)) x28 (.D(Data_In), .en(decoder_1_out0[28]), .clk(Clock), .Q(x28_q), .clr(Reset));
  Register #(.width(32)) x30 (.D(Data_In), .en(decoder_1_out0[30]), .clk(Clock), .Q(x30_q), .clr(Reset));
  Register #(.width(32)) x1 (.D(Data_In), .en(decoder_1_out0[1]), .clk(Clock), .Q(x1_q), .clr(Reset));
  Register #(.width(32)) x3 (.D(Data_In), .en(decoder_1_out0[3]), .clk(Clock), .Q(x3_q), .clr(Reset));
  Register #(.width(32)) x5 (.D(Data_In), .en(decoder_1_out0[5]), .clk(Clock), .Q(x5_q), .clr(Reset));
  Register #(.width(32)) x7 (.D(Data_In), .en(decoder_1_out0[7]), .clk(Clock), .Q(x7_q), .clr(Reset));
  Register #(.width(32)) x9 (.D(Data_In), .en(decoder_1_out0[9]), .clk(Clock), .Q(x9_q), .clr(Reset));
  Register #(.width(32)) x11 (.D(Data_In), .en(decoder_1_out0[11]), .clk(Clock), .Q(x11_q), .clr(Reset));
  Register #(.width(32)) x13 (.D(Data_In), .en(decoder_1_out0[13]), .clk(Clock), .Q(x13_q), .clr(Reset));
  Register #(.width(32)) x15 (.D(Data_In), .en(decoder_1_out0[15]), .clk(Clock), .Q(x15_q), .clr(Reset));
  Register #(.width(32)) x17 (.D(Data_In), .en(decoder_1_out0[17]), .clk(Clock), .Q(x17_q), .clr(Reset));
  Register #(.width(32)) x19 (.D(Data_In), .en(decoder_1_out0[19]), .clk(Clock), .Q(x19_q), .clr(Reset));
  Register #(.width(32)) x21 (.D(Data_In), .en(decoder_1_out0[21]), .clk(Clock), .Q(x21_q), .clr(Reset));
  Register #(.width(32)) x23 (.D(Data_In), .en(decoder_1_out0[23]), .clk(Clock), .Q(x23_q), .clr(Reset));
  Register #(.width(32)) x25 (.D(Data_In), .en(decoder_1_out0[25]), .clk(Clock), .Q(x25_q), .clr(Reset));
  Register #(.width(32)) x27 (.D(Data_In), .en(decoder_1_out0[27]), .clk(Clock), .Q(x27_q), .clr(Reset));
  Register #(.width(32)) x29 (.D(Data_In), .en(decoder_1_out0[29]), .clk(Clock), .Q(x29_q), .clr(Reset));
  Register #(.width(32)) x31 (.D(Data_In), .en(decoder_1_out0[31]), .clk(Clock), .Q(x31_q), .clr(Reset));
  Multiplexer #(.select(5), .width(32)) multiplexer_1 (
    .in0({32{1'b0}}), .in1(x1_q), .in2(x2_q), .in3(x3_q), .in4(x4_q), .in5(x5_q), .in6(x6_q), .in7(x7_q),
    .in8(x8_q), .in9(x9_q), .in10(x10_q), .in11(x11_q), .in12(x12_q), .in13(x13_q), .in14(x14_q),
    .in15(x15_q), .in16(x16_q), .in17(x17_q), .in18(x18_q), .in19(x19_q), .in20(x20_q), .in21(x21_q),
    .in22(x22_q), .in23(x23_q), .in24(x24_q), .in25(x25_q), .in26(x26_q), .in27(x27_q), .in28(x28_q),
    .in29(x29_q), .in30(x30_q), .in31(x31_q), .out(A_Data_Out), .sel(Address_A));
  Multiplexer #(.select(5), .width(32)) multiplexer_2 (
    .in0({32{1'b0}}), .in1(x1_q), .in2(x2_q), .in3(x3_q), .in4(x4_q), .in5(x5_q), .in6(x6_q), .in7(x7_q),
    .in8(x8_q), .in9(x9_q), .in10(x10_q), .in11(x11_q), .in12(x12_q), .in13(x13_q), .in14(x14_q),
    .in15(x15_q), .in16(x16_q), .in17(x17_q), .in18(x18_q), .in19(x19_q), .in20(x20_q), .in21(x21_q),
    .in22(x22_q), .in23(x23_q), .in24(x24_q), .in25(x25_q), .in26(x26_q), .in27(x27_q), .in28(x28_q),
    .in29(x29_q), .in30(x30_q), .in31(x31_q), .out(B_Data_Out), .sel(Address_B));
endmodule

module Operation_Controller (
  input  Phase1,
  input  Phase2,
  input  [31:0] Data_In,
  input  Clock,
  input  Reset,
  input  System_Load,
  input  [3:0] CNZV,
  output [14:0] Register_Adresses,
  output [2:0] Data_Type,
  output ALU_Use_PC,
  output [4:0] OP_Function,
  output Use_Immediate,
  output Register_File_Write,
  output [31:0] Current_Instruction_Out,
  output [6:0] OPCode,
  output PC_Read_Next,
  output [9:0] Current_Decoded_Instruction,
  output PC_Jump,
  output Data_IO_Write,
  output Data_IO_Read,
  output PAD_Write,
  output [31:0] Immediate,
  output PC_Relative,
  output PC_Use_Offset,
  output PAD_Read,
  output PC_Forward_Address,
  output [1:0] PAD_Data_Size,
  output Load_Upper_Immediate
);

  wire and_1_out, and_2_out, and_5_out, Floating_Point, Flush_Next_Instruction, Load, Load_Second_Part,
       multiplexer_4_out, not_1_out, not_2_out, not_3_out, or_1_out, or_2_out, or_3_out, or_4_out, or_6_out,
       or_8_out, or_10_out, xor_1_out;
  wire [4:0] Load_C_Address_q;
  wire [31:0] multiplexer_1_out, multiplexer_2_out, Next_Instruction_q;

  Multiplexer #(.width(32)) multiplexer_1 (.in0(Data_In), .in1(32'h13), .out(multiplexer_1_out), .sel(Reset));
  Register #(.width(32)) Next_Instruction (
    .D(multiplexer_1_out), .en(or_1_out), .clk(Clock), .Q(Next_Instruction_q));  // open: clr
  or or_1 (or_1_out, Phase1, Reset);
  or or_2 (or_2_out, Flush_Next_Instruction, Reset);
  Multiplexer #(.width(32)) multiplexer_2 (
    .in0(Next_Instruction_q), .in1(32'h13), .out(multiplexer_2_out), .sel(or_2_out));
  Register #(.width(32)) Current_Instruction (
    .D(multiplexer_2_out), .en(or_3_out), .clk(Clock), .Q(Current_Instruction_Out));  // open: clr
  or or_3 (or_3_out, Phase2, Reset);
  Register #(.width(1)) u_Load_Second_Part (.D(Load), .en(Phase2), .clk(Clock), .Q(Load_Second_Part), .clr(Reset));
  Register #(.width(5)) Load_C_Address (
    .D(Current_Instruction_Out[11:7]), .en(Phase2), .clk(Clock), .Q(Load_C_Address_q), .clr(Reset));
  Register #(.width(3)) Data_Type_Reg (
    .D(Current_Instruction_Out[14:12]), .en(Phase2), .clk(Clock), .Q(Data_Type), .clr(Reset));
  or or_4 (or_4_out, ALU_Use_PC, Current_Decoded_Instruction[5]);
  Multiplexer #(.width(5)) multiplexer_3 (
    .in0(Current_Instruction_Out[11:7]), .in1(Load_C_Address_q), .out(Register_Adresses[4:0]), .sel(and_1_out));
  and and_1 (and_1_out, Load_Second_Part, Phase1);
  Operation_Decoder OperationDecoder (
    .OPCODE(Current_Instruction_Out[6:0]), .IMMEDIATE(Current_Decoded_Instruction[1]),
    .LOAD(Current_Decoded_Instruction[0]), .OPERATION(Current_Decoded_Instruction[4]),
    .ADD_UPPER_IMMEDIATE_PC(ALU_Use_PC), .STORE(Current_Decoded_Instruction[3]),
    .LOAD_UPPER_IMMEDIATE(Current_Decoded_Instruction[5]), .BRANCH(Current_Decoded_Instruction[6]),
    .JUMP_AND_LINK_REGISTER(Current_Decoded_Instruction[7]), .JUMP_AND_LINK(Current_Decoded_Instruction[8]),
    .SYSTEM(Current_Decoded_Instruction[9]), .FLOATING_POINT(Floating_Point));
  Immediate_Decoder ImmediateDecoder (
    .Upper_Immediate(or_4_out), .Jump(Current_Decoded_Instruction[8]),
    .Branch(Current_Decoded_Instruction[6]), .Instruction(Current_Instruction_Out),
    .Store(Current_Decoded_Instruction[3]), .Immediate(Immediate));
  or or_5 (Load, System_Load, Current_Decoded_Instruction[0]);
  or or_6 (or_6_out, Current_Decoded_Instruction[5], ALU_Use_PC, Current_Decoded_Instruction[4], Current_Decoded_Instruction[8], Current_Decoded_Instruction[7], Current_Decoded_Instruction[9]);
  and and_2 (and_2_out, Phase2, or_6_out);
  or or_7 (Register_File_Write, and_2_out, and_5_out);
  or or_8 (or_8_out, Current_Decoded_Instruction[7], Current_Decoded_Instruction[8]);
  and and_3 (PC_Read_Next, or_8_out, Phase2);
  xor xor_1 (xor_1_out, CNZV[3], CNZV[1]);
  or or_9 (PC_Relative, Current_Decoded_Instruction[6], Current_Decoded_Instruction[8]);
  or or_10 (or_10_out, Load, Current_Decoded_Instruction[3]);
  and and_4 (PC_Forward_Address, or_10_out, Phase2);
  and and_5 (and_5_out, Phase1, Load_Second_Part);
  not not_1 (not_1_out, CNZV[2]);
  Multiplexer #(.enable("true"), .select(3)) multiplexer_4 (
    .in0(CNZV[2]), .in1(not_1_out), .in2(1'b0), .in3(1'b0), .in4(xor_1_out), .in5(not_2_out),
    .in6(not_3_out), .in7(CNZV[0]), .out(multiplexer_4_out), .sel(Current_Instruction_Out[14:12]),
    .en(Current_Decoded_Instruction[6]));
  not not_2 (not_2_out, xor_1_out);
  not not_3 (not_3_out, CNZV[0]);
  and and_6 (Load_Upper_Immediate, Current_Decoded_Instruction[5], Phase2);
  or or_11 (Flush_Next_Instruction, multiplexer_4_out, Current_Decoded_Instruction[7], Current_Decoded_Instruction[8]);
  and and_7 (PC_Jump, Flush_Next_Instruction, Phase2);
  or or_12 (Use_Immediate, Current_Decoded_Instruction[1], ALU_Use_PC);
  and and_8 (Data_IO_Write, Phase2, Load);
  or or_13 (PAD_Read, Phase1, Data_IO_Write);
  or or_14 (PAD_Data_Size[0], Current_Instruction_Out[12], Current_Instruction_Out[13]);
  Multiplexer #(.width(5)) multiplexer_5 (
    .in0(5'b10000),
    .in1({Current_Instruction_Out[30], Current_Instruction_Out[26], Current_Instruction_Out[14:12]}),
    .out(OP_Function), .sel(Current_Decoded_Instruction[4]));
  and and_9 (Data_IO_Read, Phase1, Load_Second_Part);
  and and_10 (PAD_Write, Phase2, Current_Decoded_Instruction[3]);

  assign Current_Decoded_Instruction[2] = ALU_Use_PC;
  assign OPCode = Current_Instruction_Out[6:0];
  assign PAD_Data_Size[1] = Current_Instruction_Out[13];
  assign PC_Use_Offset = Current_Decoded_Instruction[3];
  assign Register_Adresses[14:5] = Current_Instruction_Out[24:15];

  // Other names for the same wires on the sheet: Funct3[2:0] = Current_Instruction_Out[14:12];
  //   Immediate_t = Current_Decoded_Instruction[1]; Add_Upper_Immediate_PC = ALU_Use_PC;
  //   Store = Current_Decoded_Instruction[3]; Operation = Current_Decoded_Instruction[4];
  //   Load_Upper_Immediate_t = Current_Decoded_Instruction[5]; Branch = Current_Decoded_Instruction[6];
  //   Jump_Register_Relative = Current_Decoded_Instruction[7]; Jump_PC_Relative = Current_Decoded_Instruction[8];
  //   System = Current_Decoded_Instruction[9]; Funct7[6:0] = Current_Instruction_Out[31:25]; Phase1n = Phase1;
  //   Phase2n = Phase2

  // Notes on the sheet:
  //   TODO: Investigar o porque aqui precisa estar invertido =>
  //   Register File
  //   Program Counter
  //   Misc
  //   ALU And Shifter
  //   Input/Output and interface Pads
endmodule

module Operation_Decoder (
  input  [6:0] OPCODE,
  output FLOATING_POINT,
  output IMMEDIATE,
  output LOAD,
  output OPERATION,
  output ADD_UPPER_IMMEDIATE_PC,
  output STORE,
  output LOAD_UPPER_IMMEDIATE,
  output BRANCH,
  output JUMP_AND_LINK_REGISTER,
  output JUMP_AND_LINK,
  output SYSTEM
);

  wire not_1_out, not_2_out, not_3_out, not_4_out, not_5_out, or_1_out, or_2_out, or_3_out, or_4_out;

  not not_1 (not_1_out, OPCODE[6]);
  not not_2 (not_2_out, OPCODE[5]);
  not not_3 (not_3_out, OPCODE[4]);
  not not_4 (not_4_out, OPCODE[3]);
  not not_5 (not_5_out, OPCODE[2]);
  or or_1 (or_1_out, OPCODE[6], not_3_out);
  or or_2 (or_2_out, not_1_out, not_2_out);
  or or_3 (or_3_out, OPCODE[4], OPCODE[2]);
  and and_1 (IMMEDIATE, not_2_out, not_1_out, not_5_out);
  and and_2 (LOAD, not_3_out, not_2_out);
  or or_4 (or_4_out, not_1_out, not_2_out);
  and and_3 (ADD_UPPER_IMMEDIATE_PC, OPCODE[2], OPCODE[4], not_2_out);
  and and_4 (STORE, OPCODE[5], not_3_out, not_1_out);
  and and_5 (LOAD_UPPER_IMMEDIATE, OPCODE[2], OPCODE[5], OPCODE[4]);
  and and_6 (BRANCH, OPCODE[6], not_3_out, not_5_out);
  and and_7 (JUMP_AND_LINK_REGISTER, OPCODE[2], not_4_out, OPCODE[6]);
  and and_8 (JUMP_AND_LINK, OPCODE[3], OPCODE[6]);
  and and_9 (SYSTEM, OPCODE[6], OPCODE[5], OPCODE[4]);
  and and_10 (FLOATING_POINT, or_1_out, or_2_out, or_3_out);
  and and_11 (OPERATION, OPCODE[4], or_4_out, not_5_out);
endmodule

module Immediate_Decoder (
  input  Upper_Immediate,
  input  Jump,
  input  Branch,
  input  Store,
  input  [31:0] Instruction,
  output [31:0] Immediate
);

  wire [1:0] or_2_out;
  wire [11:0] multiplexer_1_out;
  wire [31:0] bit_extender_1_out, bit_extender_2_out, bit_extender_3_out;

  Multiplexer #(.width(12)) multiplexer_1 (
    .in0(Instruction[31:20]), .in1({Instruction[31:25], Instruction[11:7]}), .out(multiplexer_1_out),
    .sel(Store));
  assign bit_extender_1_out = {{19{Instruction[31]}}, {Instruction[31], Instruction[7], Instruction[30:25], Instruction[11:8], 1'b0}};  // Bit_Extender bit_extender_1
  assign bit_extender_2_out = {{11{Instruction[31]}}, {Instruction[31], Instruction[19:12], Instruction[20], Instruction[30:21], 1'b0}};  // Bit_Extender bit_extender_2
  assign bit_extender_3_out = {{20{multiplexer_1_out[11]}}, multiplexer_1_out};  // Bit_Extender bit_extender_3
  or or_1 (or_2_out[1], Upper_Immediate, Jump);
  or or_2 (or_2_out[0], Jump, Branch);
  Multiplexer #(.select(2), .width(32)) multiplexer_2 (
    .in0(bit_extender_3_out), .in1(bit_extender_1_out), .in2({Instruction[31:12], {12{1'b0}}}),
    .in3(bit_extender_2_out), .out(Immediate), .sel(or_2_out));

  // Notes on the sheet:
  //   I-type
  //   S-type
  //   B-type
  //   U-type
  //   J-type
endmodule

module Load_Store_Decoder (
  input  [6:0] OPCODE,
  output LOAD
);

  wire not_1_out, not_2_out, not_3_out, not_4_out;

  not not_1 (not_1_out, OPCODE[6]);
  not not_2 (not_2_out, OPCODE[5]);
  not not_3 (not_3_out, OPCODE[4]);
  not not_4 (not_4_out, OPCODE[3]);
  and and_1 (LOAD, not_1_out, not_2_out, not_3_out, not_4_out, OPCODE[1], OPCODE[0]);
endmodule

module Multiplication (
  input  [31:0] A,
  input  [31:0] B,
  input  [1:0] Sign,
  output [31:0] R_Low,
  output [31:0] R_High
);

  wire [32:31] multiplier_1_cout;
  wire [32:32] and_1_out, and_2_out;

  and and_1 (and_1_out[32], A[31], Sign[0]);
  and and_2 (and_2_out[32], B[31], Sign[1]);
  Multiplier #(.mode("twosComplement"), .width(33)) multiplier_1 (
    .a({and_1_out[32], A}), .b({and_2_out[32], B}), .out({R_High[0], R_Low}),
    .cout({multiplier_1_cout, R_High[31:1]}));  // open: cin
endmodule

module Address_Selector (
  input  Read_In,
  input  [31:0] Address_In,
  input  [31:0] Min_Address,
  input  [31:0] Max_Address,
  input  Write_In,
  output [31:0] Address_Out,
  output Read_Out,
  output Write_Out
);

  wire and_1_out, comparator_1_eq, comparator_1_gt, comparator_2_lt, or_1_out;

  Comparator #(.width(32)) comparator_1 (
    .a(Address_In), .b(Min_Address), .gt(comparator_1_gt), .eq(comparator_1_eq));  // open: lt
  Comparator #(.width(32)) comparator_2 (.a(Address_In), .b(Max_Address), .lt(comparator_2_lt));  // open: gt, eq
  or or_1 (or_1_out, comparator_1_gt, comparator_1_eq);
  and and_1 (and_1_out, or_1_out, comparator_2_lt);
  and and_2 (Read_Out, Read_In, and_1_out);
  and and_3 (Write_Out, and_1_out, Write_In);

  assign Address_Out = Address_In;
endmodule

module CSR_Controller (
  input  [31:0] A_Bus,
  input  Phase1,
  input  Phase2,
  input  [31:0] Current_Instruction,
  input  Reset,
  input  [31:0] Calculated_Address,
  input  Clock,
  input  PC_Jump,
  input  [31:0] Current_PC,
  input  [9:0] Current_Decoded_Instruction,
  input  Pad_Software_Interrupt,
  input  Pad_Timer_Interrupt,
  input  Pad_External_Interrupt,
  output [31:0] C_Bus,
  output System_Jump,
  output System_Load,
  output [31:0] System_Target_Address,
  output Read_CSR
);

  wire and_6_out, and_7_out, and_8_out, and_9_out, and_10_out, and_12_out, and_13_out, and_14_out,
       and_15_out, and_16_out, and_17_out, and_18_out, and_20_out, and_22_out, and_23_out, and_24_out,
       and_25_out, and_26_out, comparator_1_eq, comparator_2_eq, comparator_3_eq, comparator_4_eq,
       comparator_5_eq, comparator_6_eq, comparator_7_eq, comparator_8_eq, comparator_9_eq, comparator_10_eq,
       comparator_11_eq, comparator_12_eq, comparator_13_eq, comparator_14_eq, comparator_15_eq,
       comparator_16_eq, comparator_17_eq, comparator_18_eq, comparator_19_eq, comparator_20_eq,
       comparator_21_eq, comparator_22_eq, comparator_23_eq, decoder_1_out0, decoder_1_out1, decoder_2_out0,
       decoder_2_out1, decoder_2_out2, decoder_2_out3, decoder_3_out0, decoder_3_out1, decoder_3_out2,
       decoder_3_out3, decoder_4_out0, decoder_4_out1, ebreak, ecall, Exception, Illegal_CSR,
       Illegal_Instruction, Illegal_System, Interrupt, Interrupt_Enabled, m_cycle_carry, m_inst_ret_carry,
       Misaligned_Address, Misaligned_Data, mret, multiplexer_6_out, multiplexer_7_out, multiplexer_12_out,
       nor_1_out, nor_2_out, nor_3_out, nor_4_out, or_2_out, or_3_out, or_5_out, or_7_out, or_11_out,
       or_13_out, or_14_out, or_15_out, or_17_out, or_18_out, or_19_out, or_22_out, or_23_out, or_24_out,
       or_25_out, or_26_out, or_27_out, priority_encoder_3_gs, Privilege, Trap, Write_mstatus, Write_priv;
  wire [1:0] priority_encoder_1_out, priority_encoder_3_out;
  wire [1:1] Previous_Privilege_q;
  wire [2:0] and_27_out, mie, priority_encoder_2_out;
  wire [4:0] and_5_out, bit_extender_1_out, bit_extender_3_out, m_cause_q, m_isa_q, or_12_out;
  wire [5:0] multiplexer_9_out, multiplexer_21_out, Trap_Cause;
  wire [7:7] Prev_Interrupt_Enabled_q;
  wire [29:0] adder_1_out, bit_extender_2_out, multiplexer_8_out;
  wire [31:0] and_21_out, bit_extender_4_out, bit_extender_5_out, m_cycle_h_q, m_cycle_q, m_inst_ret_h_q,
       m_inst_ret_q, m_scratch_q, m_t_val_q, m_t_vec, multiplexer_1_out, multiplexer_2_out,
       multiplexer_4_out, multiplexer_5_out, multiplexer_10_out, multiplexer_11_out, multiplexer_13_out,
       multiplexer_14_out, multiplexer_15_out, multiplexer_16_out, multiplexer_17_out, multiplexer_18_out,
       multiplexer_19_out, multiplexer_22_out, or_20_out, Trap_Value;
  wire [31:2] m_e_pc;
  wire [31:31] m_cause_interrupt_q;

  nor nor_1 (nor_1_out, Current_Instruction[12], Current_Instruction[13], Current_Instruction[14]);
  Comparator #(.width(12)) comparator_1 (
    .a(Current_Instruction[31:20]), .b({12{1'b0}}), .eq(comparator_1_eq));  // open: gt, lt
  Comparator #(.width(12)) comparator_2 (
    .a(Current_Instruction[31:20]), .b(12'h1), .eq(comparator_2_eq));  // open: gt, lt
  Comparator #(.width(12)) comparator_3 (
    .a(Current_Instruction[31:20]), .b(12'h302), .eq(comparator_3_eq));  // open: gt, lt
  and and_1 (mret, Current_Decoded_Instruction[9], comparator_3_eq, nor_1_out);
  Comparator #(.width(12)) comparator_4 (
    .a(Current_Instruction[31:20]), .b(12'h300), .eq(comparator_4_eq));  // open: gt, lt
  Comparator #(.width(12)) comparator_5 (
    .a(Current_Instruction[31:20]), .b(12'h304), .eq(comparator_5_eq));  // open: gt, lt
  Comparator #(.width(12)) comparator_6 (
    .a(Current_Instruction[31:20]), .b(12'h310), .eq(comparator_6_eq));  // open: gt, lt
  Comparator #(.width(12)) comparator_7 (
    .a(Current_Instruction[31:20]), .b(12'h341), .eq(comparator_7_eq));  // open: gt, lt
  Comparator #(.width(12)) comparator_8 (
    .a(Current_Instruction[31:20]), .b(12'h343), .eq(comparator_8_eq));  // open: gt, lt
  Comparator #(.width(12)) comparator_9 (
    .a(Current_Instruction[31:20]), .b(12'hc00), .eq(comparator_9_eq));  // open: gt, lt
  Comparator #(.width(12)) comparator_10 (
    .a(Current_Instruction[31:20]), .b(12'hc02), .eq(comparator_10_eq));  // open: gt, lt
  Comparator #(.width(12)) comparator_11 (
    .a(Current_Instruction[31:20]), .b(12'hc81), .eq(comparator_11_eq));  // open: gt, lt
  Comparator #(.width(12)) comparator_12 (
    .a(Current_Instruction[31:20]), .b(12'hf11), .eq(comparator_12_eq));  // open: gt, lt
  Comparator #(.width(12)) comparator_13 (
    .a(Current_Instruction[31:20]), .b(12'hf13), .eq(comparator_13_eq));  // open: gt, lt
  and and_2 (ecall, Current_Decoded_Instruction[9], comparator_2_eq, nor_1_out);
  and and_3 (ebreak, Current_Decoded_Instruction[9], comparator_1_eq, nor_1_out);
  Comparator #(.width(12)) comparator_14 (
    .a(Current_Instruction[31:20]), .b(12'h301), .eq(comparator_14_eq));  // open: gt, lt
  Comparator #(.width(12)) comparator_15 (
    .a(Current_Instruction[31:20]), .b(12'h305), .eq(comparator_15_eq));  // open: gt, lt
  Comparator #(.width(12)) comparator_16 (
    .a(Current_Instruction[31:20]), .b(12'h340), .eq(comparator_16_eq));  // open: gt, lt
  Comparator #(.width(12)) comparator_17 (
    .a(Current_Instruction[31:20]), .b(12'h342), .eq(comparator_17_eq));  // open: gt, lt
  Comparator #(.width(12)) comparator_18 (
    .a(Current_Instruction[31:20]), .b(12'h344), .eq(comparator_18_eq));  // open: gt, lt
  Comparator #(.width(12)) comparator_19 (
    .a(Current_Instruction[31:20]), .b(12'hc01), .eq(comparator_19_eq));  // open: gt, lt
  Comparator #(.width(12)) comparator_20 (
    .a(Current_Instruction[31:20]), .b(12'hc80), .eq(comparator_20_eq));  // open: gt, lt
  Comparator #(.width(12)) comparator_21 (
    .a(Current_Instruction[31:20]), .b(12'hc82), .eq(comparator_21_eq));  // open: gt, lt
  Comparator #(.width(12)) comparator_22 (
    .a(Current_Instruction[31:20]), .b(12'hf12), .eq(comparator_22_eq));  // open: gt, lt
  Comparator #(.width(12)) comparator_23 (
    .a(Current_Instruction[31:20]), .b(12'hf14), .eq(comparator_23_eq));  // open: gt, lt
  or or_1 (Misaligned_Address, Calculated_Address[0], Calculated_Address[1]);
  or or_2 (or_2_out, Current_Instruction[12], Current_Instruction[13]);
  or or_3 (or_3_out, comparator_1_eq, comparator_2_eq, comparator_3_eq);
  and and_4 (Illegal_System, ~or_3_out, nor_1_out);  // AND_Gate
  assign bit_extender_1_out = {{4{m_t_vec[0]}}, m_t_vec[0]};  // Bit_Extender bit_extender_1
  assign and_5_out = bit_extender_1_out & Trap_Cause[4:0];  // AND_Gate and_5, 5 bits wide
  or or_4 (Read_CSR, Current_Instruction[12], Current_Instruction[13]);
  nor nor_2 (nor_2_out, Current_Instruction[12], Current_Instruction[13], Current_Instruction[14]);
  and and_6 (and_6_out, Misaligned_Address, Current_Instruction[13]);
  and and_7 (and_7_out, Calculated_Address[0], Calculated_Address[1], or_2_out);
  nor nor_3 (nor_3_out, comparator_4_eq, comparator_14_eq, comparator_5_eq, comparator_15_eq, comparator_6_eq, comparator_16_eq, comparator_7_eq, comparator_17_eq, comparator_8_eq, comparator_18_eq, comparator_9_eq, comparator_19_eq, comparator_10_eq, comparator_20_eq, comparator_11_eq, comparator_21_eq, comparator_12_eq, comparator_22_eq, comparator_13_eq, comparator_23_eq);
  or or_5 (or_5_out, comparator_19_eq, comparator_11_eq);
  Multiplexer #(.width(32)) multiplexer_1 (
    .in0(32'h81000000), .in1(32'h81000004), .out(multiplexer_1_out), .sel(comparator_11_eq));
  Multiplexer #(.width(32)) multiplexer_2 (
    .in0({m_e_pc, 2'b00}), .in1(multiplexer_1_out), .out(multiplexer_2_out), .sel(System_Load));
  assign bit_extender_2_out = {{25{and_5_out[4]}}, and_5_out};  // Bit_Extender bit_extender_2
  nor nor_4 (nor_4_out, Current_Decoded_Instruction[0], Current_Decoded_Instruction[1], Current_Decoded_Instruction[2], Current_Decoded_Instruction[3], Current_Decoded_Instruction[4], Current_Decoded_Instruction[5], Current_Decoded_Instruction[6], Current_Decoded_Instruction[7], Current_Decoded_Instruction[8], Current_Decoded_Instruction[9]);
  and and_8 (and_8_out, Illegal_CSR, Read_CSR);
  and and_9 (and_9_out, nor_2_out, Illegal_System);
  or or_6 (Misaligned_Data, and_6_out, and_7_out);
  and and_10 (and_10_out, ~Privilege, Current_Instruction[28]);  // AND_Gate
  and and_11 (System_Load, or_5_out, Read_CSR);
  or or_7 (or_7_out, mret, Exception, Interrupt);
  Adder #(.width(30)) adder_1 (.a(m_t_vec[31:2]), .b(bit_extender_2_out), .out(adder_1_out));  // open: cin, cout
  and and_12 (and_12_out, Current_Decoded_Instruction[9], and_8_out);
  and and_13 (and_13_out, Current_Decoded_Instruction[9], and_9_out);
  or or_8 (Illegal_CSR, and_10_out, nor_3_out);
  and and_14 (and_14_out, mret, Phase2);
  or or_9 (System_Jump, and_14_out, Trap);
  Priority_Encoder #(.select(2)) priority_encoder_1 (
    .in0(1'b0), .in1(mret), .in2(Exception), .in3(Interrupt), .out(priority_encoder_1_out), .en_in(or_7_out));  // open: gs, en_out
  Multiplexer #(.select(2), .width(32)) multiplexer_3 (
    .in0(multiplexer_2_out), .in1({m_e_pc, 2'b00}), .in2({m_t_vec[31:2], 2'b00}), .in3({adder_1_out, 2'b00}),
    .out(System_Target_Address), .sel(priority_encoder_1_out));
  or or_10 (Illegal_Instruction, nor_4_out, and_12_out, and_13_out);
  and and_15 (and_15_out, Phase2, ~Illegal_CSR, Read_CSR);  // AND_Gate
  and and_16 (and_16_out, and_15_out, ~Current_Instruction[30], Current_Instruction[28]);  // AND_Gate
  Decoder decoder_1 (.out0(decoder_1_out0), .out1(decoder_1_out1), .sel(Current_Instruction[26]), .en(and_16_out));
  and and_17 (and_17_out, decoder_1_out1, ~Current_Instruction[22]);  // AND_Gate
  Decoder #(.select(2)) decoder_2 (
    .out0(decoder_2_out0), .out1(decoder_2_out1), .out2(decoder_2_out2), .out3(decoder_2_out3),
    .sel({Current_Instruction[22], Current_Instruction[20]}), .en(decoder_1_out0));
  Decoder #(.select(2)) decoder_3 (
    .out0(decoder_3_out0), .out1(decoder_3_out1), .out2(decoder_3_out2), .out3(decoder_3_out3),
    .sel(Current_Instruction[21:20]), .en(and_17_out));
  assign bit_extender_3_out = {{4{Reset}}, Reset};  // Bit_Extender bit_extender_3
  assign bit_extender_4_out = {{27{1'b0}}, Current_Instruction[24:20]};  // Bit_Extender bit_extender_4
  and and_18 (and_18_out, Privilege, Trap);
  or or_11 (or_11_out, Interrupt_Enabled, ~Trap);  // OR_Gate
  assign or_12_out = bit_extender_3_out | {multiplexer_11_out[30], multiplexer_11_out[20], multiplexer_11_out[12], multiplexer_11_out[8], multiplexer_11_out[4]};  // OR_Gate or_12, 5 bits wide
  or or_13 (or_13_out, decoder_2_out1, Reset);
  Multiplexer #(.width(32)) multiplexer_4 (
    .in0(multiplexer_11_out), .in1(32'h80000001), .out(multiplexer_4_out), .sel(Reset));
  or or_14 (or_14_out, decoder_2_out3, Reset);
  Multiplexer #(.width(32)) multiplexer_5 (
    .in0(A_Bus), .in1(bit_extender_4_out), .out(multiplexer_5_out), .sel(Current_Instruction[14]));
  Multiplexer multiplexer_6 (.in0(and_18_out), .in1(multiplexer_11_out[12]), .out(multiplexer_6_out), .sel(Read_CSR));
  Multiplexer multiplexer_7 (.in0(or_11_out), .in1(multiplexer_11_out[7]), .out(multiplexer_7_out), .sel(Read_CSR));
  or or_15 (or_15_out, Exception, Interrupt);
  Multiplexer #(.width(30)) multiplexer_8 (
    .in0(multiplexer_11_out[31:2]), .in1(Current_PC[31:2]), .out(multiplexer_8_out), .sel(Trap));
  Multiplexer #(.width(6)) multiplexer_9 (
    .in0({multiplexer_11_out[31], multiplexer_11_out[4:0]}), .in1(Trap_Cause), .out(multiplexer_9_out),
    .sel(Trap));
  Multiplexer #(.width(32)) multiplexer_10 (
    .in0(multiplexer_11_out), .in1(Trap_Value), .out(multiplexer_10_out), .sel(Trap));
  Register #(.width(1)) Previous_Privilege (
    .D(multiplexer_6_out), .en(Write_mstatus), .clk(Clock), .Q(Previous_Privilege_q[1]), .clr(Reset));
  Register #(.width(1)) Prev_Interrupt_Enabled (
    .D(multiplexer_7_out), .en(Write_mstatus), .clk(Clock), .Q(Prev_Interrupt_Enabled_q[7]), .clr(Reset));
  and and_19 (Trap, Phase2, or_15_out);
  Register #(.width(30)) u_m_t_vec (
    .D(multiplexer_4_out[31:2]), .en(or_14_out), .clk(Clock), .Q(m_t_vec[31:2]));  // open: clr
  Multiplexer #(.select(2), .width(32)) multiplexer_11 (
    .in0(multiplexer_5_out), .in1(multiplexer_5_out), .in2(or_20_out), .in3(and_21_out),
    .out(multiplexer_11_out), .sel(Current_Instruction[13:12]));
  or or_16 (Write_priv, Trap, mret);
  Register #(.width(5)) m_isa (
    .D({or_12_out[4:1], or_12_out[1]}), .en(or_13_out), .clk(Clock), .Q(m_isa_q));  // open: clr
  Register #(.width(3)) m_i_e (
    .D({multiplexer_11_out[11], multiplexer_11_out[7], multiplexer_11_out[3]}), .en(decoder_2_out2),
    .clk(Clock), .Q(mie), .clr(Reset));
  Register #(.width(1)) m_t_vec_vectored (
    .D(multiplexer_4_out[0]), .en(or_14_out), .clk(Clock), .Q(m_t_vec[0]));  // open: clr
  Register #(.width(32)) m_scratch (
    .D(multiplexer_11_out), .en(decoder_3_out0), .clk(Clock), .Q(m_scratch_q), .clr(Reset));
  Register #(.width(30)) u_m_e_pc (.D(multiplexer_8_out), .en(or_17_out), .clk(Clock), .Q(m_e_pc), .clr(Reset));
  or or_17 (or_17_out, Trap, decoder_3_out1);
  or or_18 (or_18_out, Trap, decoder_3_out2);
  Register #(.width(5)) m_cause (.D(multiplexer_9_out[4:0]), .en(or_18_out), .clk(Clock), .Q(m_cause_q), .clr(Reset));
  Register #(.width(32)) m_t_val (.D(multiplexer_10_out), .en(or_19_out), .clk(Clock), .Q(m_t_val_q), .clr(Reset));
  or or_19 (or_19_out, Trap, decoder_3_out3);
  Counter #(.max('hffffffff), .width(32)) m_cycle (
    .count(1'b1), .Q(m_cycle_q), .carry(m_cycle_carry), .clk(Clock), .clr(Reset));  // open: load, D, up
  and and_20 (and_20_out, Phase2, ~Exception);  // AND_Gate
  Counter #(.max('hffffffff), .width(32)) m_inst_ret (
    .count(and_20_out), .Q(m_inst_ret_q), .carry(m_inst_ret_carry), .clk(Clock), .clr(Reset));  // open: load, D, up
  assign or_20_out = multiplexer_5_out | C_Bus;  // OR_Gate or_20, 32 bits wide
  assign and_21_out = ~multiplexer_5_out & C_Bus;  // AND_Gate and_21, 32 bits wide
  or or_21 (Write_mstatus, decoder_2_out0, Write_priv);
  Register #(.width(1)) m_cause_interrupt (
    .D(multiplexer_9_out[5]), .en(or_18_out), .clk(Clock), .Q(m_cause_interrupt_q[31]), .clr(Reset));
  or or_22 (or_22_out, Previous_Privilege_q[1], Trap, Reset);
  and and_22 (and_22_out, Prev_Interrupt_Enabled_q[7], ~Trap);  // AND_Gate
  Multiplexer multiplexer_12 (.in0(and_22_out), .in1(multiplexer_11_out[3]), .out(multiplexer_12_out), .sel(Read_CSR));
  Counter #(.max('hffffffff), .width(32)) m_cycle_h (
    .count(m_cycle_carry), .Q(m_cycle_h_q), .clk(Clock), .clr(Reset));  // open: load, D, carry, up
  Counter #(.max('hffffffff), .width(32)) m_inst_ret_h (
    .count(m_inst_ret_carry), .Q(m_inst_ret_h_q), .clk(Clock), .clr(Reset));  // open: load, D, carry, up
  Register #(.width(1)) u_Privilege (.D(or_22_out), .en(or_23_out), .clk(Clock), .Q(Privilege));  // open: clr
  or or_23 (or_23_out, Write_priv, Reset);
  Register #(.width(1)) u_Interrupt_Enabled (
    .D(multiplexer_12_out), .en(Write_mstatus), .clk(Clock), .Q(Interrupt_Enabled), .clr(Reset));
  Multiplexer #(.select(2), .width(32)) multiplexer_13 (
    .in0({{19{1'b0}}, {2{Previous_Privilege_q[1]}}, 3'b000, Prev_Interrupt_Enabled_q[7], 3'b000, Interrupt_Enabled, 3'b000}),
    .in1({1'b0, m_isa_q[4], {9{1'b0}}, m_isa_q[3], {7{1'b0}}, m_isa_q[2], 3'b000, m_isa_q[1], 3'b000, m_isa_q[0], 4'b0000}),
    .in2({{20{1'b0}}, mie[2], 3'b000, mie[1], 3'b000, mie[0], 3'b000}),
    .in3({m_t_vec[31:2], 1'b0, m_t_vec[0]}), .out(multiplexer_13_out),
    .sel({Current_Instruction[22], Current_Instruction[20]}));
  Multiplexer #(.select(2), .width(32)) multiplexer_14 (
    .in0(m_scratch_q), .in1({m_e_pc, 2'b00}), .in2({m_cause_interrupt_q[31], {26{1'b0}}, m_cause_q}),
    .in3(m_t_val_q), .out(multiplexer_14_out), .sel(Current_Instruction[21:20]));
  Multiplexer #(.select(2), .width(32)) multiplexer_15 (
    .in0({32{1'b0}}), .in1(32'haf001d), .in2(32'hf0f0f0f0), .in3(32'h4), .out(multiplexer_15_out),
    .sel(Current_Instruction[21:20]));
  Multiplexer #(.width(32)) multiplexer_16 (
    .in0(multiplexer_14_out),
    .in1({{20{1'b0}}, Pad_External_Interrupt, 3'b000, Pad_Timer_Interrupt, 3'b000, Pad_Software_Interrupt, 3'b000}),
    .out(multiplexer_16_out), .sel(Current_Instruction[22]));
  Multiplexer #(.select(2), .width(32)) multiplexer_17 (
    .in0(m_cycle_q), .in1(m_inst_ret_q), .in2(m_cycle_h_q), .in3(m_inst_ret_h_q), .out(multiplexer_17_out),
    .sel({Current_Instruction[27], Current_Instruction[21]}));
  Multiplexer #(.width(32)) multiplexer_18 (
    .in0(multiplexer_13_out), .in1(multiplexer_16_out), .out(multiplexer_18_out),
    .sel(Current_Instruction[26]));
  Multiplexer #(.width(32)) multiplexer_19 (
    .in0(multiplexer_17_out), .in1(multiplexer_15_out), .out(multiplexer_19_out),
    .sel(Current_Instruction[28]));
  Multiplexer #(.width(32)) multiplexer_20 (
    .in0(multiplexer_18_out), .in1(multiplexer_19_out), .out(C_Bus), .sel(Current_Instruction[30]));
  Decoder decoder_4 (.out0(decoder_4_out0), .out1(decoder_4_out1), .sel(Privilege), .en(ecall));
  and and_23 (and_23_out, PC_Jump, Current_Decoded_Instruction[6]);
  or or_24 (or_24_out, and_23_out, Current_Decoded_Instruction[7], Current_Decoded_Instruction[8]);
  and and_24 (and_24_out, Misaligned_Data, Current_Decoded_Instruction[3]);
  and and_25 (and_25_out, Misaligned_Data, Current_Decoded_Instruction[0]);
  and and_26 (and_26_out, Misaligned_Address, or_24_out);
  or or_25 (or_25_out, and_24_out, and_25_out, decoder_4_out0, decoder_4_out1, ebreak, and_26_out, Illegal_Instruction);
  assign and_27_out = {Pad_External_Interrupt, Pad_Timer_Interrupt, Pad_Software_Interrupt} & mie;  // AND_Gate and_27, 3 bits wide
  Priority_Encoder priority_encoder_2 (
    .in0(1'b0), .in1(and_24_out), .in2(and_25_out), .in3(decoder_4_out0), .in4(decoder_4_out1), .in5(ebreak),
    .in6(and_26_out), .in7(Illegal_Instruction), .out(priority_encoder_2_out), .en_in(or_25_out),
    .gs(Exception));  // open: en_out
  Multiplexer #(.select(3), .width(6)) multiplexer_21 (
    .in0({6{1'b0}}), .in1(6'b000110), .in2(6'b000100), .in3(6'b001000), .in4(6'b001011), .in5(6'b000011),
    .in6({6{1'b0}}), .in7(6'b000010), .out(multiplexer_21_out), .sel(priority_encoder_2_out));
  or or_26 (or_26_out, Interrupt_Enabled, ~Privilege);  // OR_Gate
  Priority_Encoder #(.select(2)) priority_encoder_3 (
    .in0(1'b0), .in1(and_27_out[0]), .in2(and_27_out[1]), .in3(and_27_out[2]), .out(priority_encoder_3_out),
    .gs(priority_encoder_3_gs), .en_in(or_27_out));  // open: en_out
  or or_27 (or_27_out, and_27_out[2], and_27_out[1], and_27_out[0]);
  Multiplexer #(.select(3), .width(32)) multiplexer_22 (
    .in0({32{1'b0}}), .in1(Calculated_Address), .in2(Calculated_Address), .in3({32{1'b0}}), .in4({32{1'b0}}),
    .in5({32{1'b0}}), .in6(Calculated_Address), .in7(Current_Instruction), .out(multiplexer_22_out),
    .sel(priority_encoder_2_out));
  and and_28 (Interrupt, or_26_out, priority_encoder_3_gs);
  Multiplexer #(.select(2), .width(6)) multiplexer_23 (
    .in0(multiplexer_21_out), .in1(6'b100111), .in2(6'b100011), .in3(6'b101011), .out(Trap_Cause),
    .sel(priority_encoder_3_out));
  assign bit_extender_5_out = {{31{Interrupt}}, Interrupt};  // Bit_Extender bit_extender_5
  assign Trap_Value = ~bit_extender_5_out & multiplexer_22_out;  // AND_Gate and_29, 32 bits wide

  // Other names for the same wires on the sheet: mip[2:0] = {Pad_External_Interrupt, Pad_Timer_Interrupt, Pad_Software_Interrupt};
  //   Load = Current_Decoded_Instruction[0]; Store = Current_Decoded_Instruction[3];
  //   Branch = Current_Decoded_Instruction[6]; Jump_And_Link_Register = Current_Decoded_Instruction[7];
  //   Jump_And_Link = Current_Decoded_Instruction[8]; System = Current_Decoded_Instruction[9];
  //   OPCode[6:0] = Current_Instruction[6:0]; Funct_3[2:0] = Current_Instruction[14:12];
  //   C_Address[4:0] = Current_Instruction[24:20]; Funct_12[11:0] = Current_Instruction[31:20];
  //   Funct_7[6:0] = Current_Instruction[31:25]; Write_CSR = Read_CSR

  // Notes on the sheet:
  //   m_hart_id
  //   m_vendor_id
  //   m_arch_id
  //   m_imp_id
  //   m_status
  //   m_i_p
endmodule

module Register_History_Generator (
  input  [31:0] Current_Value,
  input  [4:0] Current_Address,
  input  [4:0] Target_Address,
  input  Write_Signal,
  input  Reset,
  input  Clock,
  output Out_Clock,
  output [15:0] Out_Value
);

  wire and_1_out, comparator_1_eq, comparator_2_gt;
  wire [3:0] counter_1_q;
  wire [31:0] Last_Value_q, register_1_q;

  Comparator #(.width(5)) comparator_1 (.a(Current_Address), .b(Target_Address), .eq(comparator_1_eq));  // open: gt, lt
  and and_1 (and_1_out, comparator_1_eq, Write_Signal);
  Register #(.trigger("falling"), .width(32)) register_1 (
    .D(Current_Value), .en(and_1_out), .clk(Clock), .Q(register_1_q));  // open: clr
  Register #(.trigger("falling"), .width(32)) Last_Value (
    .D(Current_Value), .en(and_1_out), .clk(Clock), .Q(Last_Value_q), .clr(Reset));
  and and_2 (Out_Clock, and_1_out, Clock);
  Comparator #(.width(32)) comparator_2 (.a(register_1_q), .b(Last_Value_q), .gt(comparator_2_gt));  // open: eq, lt
  Counter #(.max('hf), .width(4)) counter_1 (
    .clr(Reset), .up(comparator_2_gt), .count(and_1_out), .clk(Clock), .Q(counter_1_q));  // open: load, D, carry
  Decoder #(.enable("false"), .select(4)) decoder_1 (
    .out0(Out_Value[0]), .out1(Out_Value[1]), .out2(Out_Value[2]), .out3(Out_Value[3]), .out4(Out_Value[4]),
    .out5(Out_Value[5]), .out6(Out_Value[6]), .out7(Out_Value[7]), .out8(Out_Value[8]), .out9(Out_Value[9]),
    .out10(Out_Value[10]), .out11(Out_Value[11]), .out12(Out_Value[12]), .out13(Out_Value[13]),
    .out14(Out_Value[14]), .out15(Out_Value[15]), .sel(counter_1_q));
endmodule

module Real_Time_Device (
  input  [31:0] Data_In,
  input  Clock,
  input  Reset,
  input  Write,
  input  [1:0] Address,
  output Timer_Interrupt,
  output [31:0] Data_Out
);

  wire and_1_out, buffer_1_out, buffer_2_out, decoder_1_out0, decoder_1_out1, decoder_1_out2, decoder_1_out3,
       m_time_carry, not_1_out, or_1_out;
  wire [63:0] m_cmp_time_q, m_time_q;

  Decoder #(.select(2)) decoder_1 (
    .out0(decoder_1_out0), .out1(decoder_1_out1), .out2(decoder_1_out2), .out3(decoder_1_out3),
    .sel(Address), .en(Write));
  buf buffer_1 (buffer_1_out, Clock);
  buf buffer_2 (buffer_2_out, buffer_1_out);
  and and_1 (and_1_out, buffer_2_out, not_1_out);
  not not_1 (not_1_out, Clock);
  or or_1 (or_1_out, and_1_out, Clock);
  Register #(.width(32)) m_cmp_time (
    .D(Data_In), .en(decoder_1_out2), .clk(Clock), .Q(m_cmp_time_q[31:0]), .clr(Reset));
  Counter #(.max('hffffffff), .width(32)) m_time (
    .load(decoder_1_out0), .D(Data_In), .count(1'b1), .Q(m_time_q[31:0]), .carry(m_time_carry),
    .clk(or_1_out), .clr(Reset));  // open: up
  Register #(.width(32)) m_cmp_time_h (
    .D(Data_In), .en(decoder_1_out3), .clk(Clock), .Q(m_cmp_time_q[63:32]), .clr(Reset));
  Counter #(.max('hffffffff), .width(32)) m_time_h (
    .load(decoder_1_out1), .D(Data_In), .count(m_time_carry), .Q(m_time_q[63:32]), .clk(or_1_out), .clr(Reset));  // open: carry, up
  Multiplexer #(.select(2), .width(32)) multiplexer_1 (
    .in0(m_time_q[31:0]), .in1(m_time_q[63:32]), .in2(m_cmp_time_q[31:0]), .in3(m_cmp_time_q[63:32]),
    .out(Data_Out), .sel(Address));
  Comparator #(.mode("unsigned"), .width(64)) comparator_1 (
    .a(m_time_q), .b(m_cmp_time_q), .gt(Timer_Interrupt));  // open: eq, lt
endmodule
